// Logisim project Cpu_8_bit.circ as structural Verilog: 21 circuits, main circuit CPU_8_BIT
module main (
  input  ON_BUTTON,
  input  RESET_BUTTON,
  input  [7:0] in_3,
  input  MAIN_CLOCK,
  input  CLOCK_2,
  input  [15:0] INSTRUCTION,
  output out_7,
  output out_8,
  output [15:0] DATA_MEM_ADDR,
  output out_10,
  output [7:0] DATA_MEM_DATA,
  output I_O_ENABLE,
  output I_O_OP,
  output DATA_IN_OUT_CTRL,
  output [7:0] DATA_TO_OUT,
  output [15:0] INSTR_MEM_ADDR
);

  wire ALU_ENABLE, BRANCH_CTRL, CARRY_FLAG, DATA_MEM_OP, EXCEPTION, exception_control_unit_1_exception,
       OVERFLOW_FLAG, PC_OVERFLOW, REG_READ_ENABLE, REG_WRITE_ENABLE, SIGN_FLAG, UPC_ENABLE, ZERO_FLAG;
  wire [2:0] ALU_OPERATION_CTRL, REG_DST, REG_SRC1, REG_SRC2, REG_WRITE_CTRL;
  wire [4:0] OP_CODE;
  wire [7:0] ALU_RESULT, CONST_VALUE, DATA_FROM_STACK, DATA_SRC2, REG_N_7;
  wire [10:0] BRANCH_OFFSET;
  wire [15:0] NEXT_PC, PC, Update_pc_unit_next_pc;

  Upgrading_pc_unit Update_pc_unit (
    .PC(PC), .BRANCH_OFFSET(BRANCH_OFFSET), .BRANCH_CTRL(BRANCH_CTRL), .UPC_ENABLE(UPC_ENABLE),
    .NEXT_PC(Update_pc_unit_next_pc), .out_5(PC_OVERFLOW));
  Multiplexer #(.width(16)) multiplexer_1 (
    .in0(Update_pc_unit_next_pc), .in1(16'h1), .out(NEXT_PC), .sel(RESET_BUTTON), .en(1'b1));
  Register #(.width(16)) Program_Counter (.D(NEXT_PC), .Q(PC), .clk(MAIN_CLOCK), .clr(EXCEPTION));  // open: en
  Multiplexer #(.width(16)) multiplexer_2 (
    .in0(PC), .in1({16{1'b0}}), .out(INSTR_MEM_ADDR), .sel(EXCEPTION), .en(1'b1));
  Instruction_management Instruction_decode (
    .INSTRUCTION(INSTRUCTION), .op_code(OP_CODE), .REG_DST(REG_DST), .REG_SRC1(REG_SRC1),
    .REG_SRC2(REG_SRC2), .BRANCH_OFFSET(BRANCH_OFFSET), .CONST_VALUE(CONST_VALUE));
  Control_unit control_unit_1 (
    .in_2(OP_CODE[4]), .in_3(OP_CODE[3]), .in_4(OP_CODE[2]), .in_5(OP_CODE[1]), .in_6(OP_CODE[0]),
    .in_1(MAIN_CLOCK), .in_7(EXCEPTION), .in_8(OVERFLOW_FLAG), .in_9(CARRY_FLAG), .in_10(ZERO_FLAG),
    .in_11(SIGN_FLAG), .DATA_MEM_L_W(out_7), .DATA_MEM_ENABLE(out_8), .DATA_MEM_OP(DATA_MEM_OP),
    .REG_R_ENABLE(REG_READ_ENABLE), .REG_W_ENABLE(REG_WRITE_ENABLE), .INSTR_MEM_ENABLE(out_10),
    .BRANCH_CTRL(BRANCH_CTRL), .UPC_ENABLE(UPC_ENABLE), .I_O_OP(I_O_OP), .I_O_ENABLE(I_O_ENABLE),
    .ALU_ENABLE(ALU_ENABLE), .REG_W_CTRL(REG_WRITE_CTRL), .out_14(ALU_OPERATION_CTRL), .in_12(RESET_BUTTON),
    .DATA_IN_CTRL(DATA_IN_OUT_CTRL));
  Register_File register_file_1 (
    .CLOCK(MAIN_CLOCK), .DATA_FROM_STACK(DATA_FROM_STACK), .DATA_FROM_ALU(ALU_RESULT),
    .CONST_VALUE(CONST_VALUE), .REG_WRITE_CTRL(REG_WRITE_CTRL), .DATA_SRC1(DATA_TO_OUT),
    .REG_READ_ENABLE(REG_READ_ENABLE), .REG_WRITE_ENABLE(REG_WRITE_ENABLE), .REG_SRC1(REG_SRC1),
    .DATA_SRC2(DATA_SRC2), .REG_SRC2(REG_SRC2), .REG_DST(REG_DST), .DATA_FROM_MEMORY(in_3),
    .DATA_FROM_REG(DATA_TO_OUT), .reg_n_7(REG_N_7), .DATA_MEM_OP(DATA_MEM_OP), .clock_2(CLOCK_2),
    .RESET_BUTTON(RESET_BUTTON));
  Exception_Control_Unit exception_control_unit_1 (
    .op_code_4(OP_CODE[4]), .op_code_3(OP_CODE[3]), .main_clock(MAIN_CLOCK), .op_code_2(OP_CODE[2]),
    .clock_2(CLOCK_2), .exception(exception_control_unit_1_exception), .op_code_1(OP_CODE[1]),
    .op_code_0(OP_CODE[0]), .overflow_flag(OVERFLOW_FLAG), .pc_overflow(PC_OVERFLOW), .stack_overflow(1'b0));
  Multiplexer multiplexer_3 (
    .in0(1'b0), .in1(exception_control_unit_1_exception), .out(EXCEPTION), .sel(ON_BUTTON), .en(1'b1));
  Data_memory_management data_memory_management_1 (
    .DATA_TO_MEMORY(DATA_TO_OUT), .DATA_TO_MEMORY_2(DATA_MEM_DATA), .reg_n_7(REG_N_7),
    .const_value(CONST_VALUE), .addr(DATA_MEM_ADDR));
  ALU alu_1 (
    .ALU_IN1(DATA_TO_OUT), .ALU_IN2(DATA_SRC2), .ALU_RESULT(ALU_RESULT), .ALU_ENABLE(ALU_ENABLE),
    .ALU_OPERATION_CTRL(ALU_OPERATION_CTRL), .ZERO_FLAG(ZERO_FLAG), .SIGN_FLAG(SIGN_FLAG),
    .CARRY_FLAG(CARRY_FLAG), .OVERFLOW_FLAG(OVERFLOW_FLAG));

  // Other names for the same wires on the sheet: DATA_FROM_MEMORY[7:0] = in_3; DATA_L_W = out_7;
  //   DATA_MEMORY_ENABLE = out_8; DATA_SRC1[7:0] = DATA_TO_OUT; INSTR_MEM_ENABLE = out_10; RESET = RESET_BUTTON
endmodule

// CONTROL_UNIT
module Control_unit (
  input  in_1,
  input  in_2,
  input  in_3,
  input  in_4,
  input  in_5,
  input  in_6,
  input  in_7,
  input  in_8,
  input  in_9,
  input  in_10,
  input  in_11,
  input  in_12,
  output ALU_ENABLE,
  output [2:0] out_14,
  output I_O_ENABLE,
  output I_O_OP,
  output DATA_IN_CTRL,
  output UPC_ENABLE,
  output BRANCH_CTRL,
  output INSTR_MEM_ENABLE,
  output [2:0] REG_W_CTRL,
  output REG_W_ENABLE,
  output REG_R_ENABLE,
  output DATA_MEM_OP,
  output DATA_MEM_L_W,
  output DATA_MEM_ENABLE
);

  wire d_ff_1_q, d_ff_2_q, d_ff_3_q, d_ff_4_q;

  D_Flip_Flop d_ff_1 (.clk(in_1), .D(in_10), .Q(d_ff_1_q), .reset(in_12));  // open: Qn, preset, en
  D_Flip_Flop d_ff_2 (.clk(in_1), .D(in_11), .Q(d_ff_2_q), .reset(in_12));  // open: Qn, preset, en
  D_Flip_Flop d_ff_3 (.clk(in_1), .D(in_9), .Q(d_ff_3_q), .reset(in_12));  // open: Qn, preset, en
  D_Flip_Flop d_ff_4 (.clk(in_1), .D(in_8), .Q(d_ff_4_q), .reset(in_12));  // open: Qn, preset, en
  Reg_File_Control_Unit reg_file_control_unit_1 (
    .op_code_4(in_2), .reg_w_ctrl_2(REG_W_CTRL[2]), .op_code_3(in_3), .reg_w_ctrl_1(REG_W_CTRL[1]),
    .op_code_2(in_4), .reg_w_ctrl_0(REG_W_CTRL[0]), .op_code_1(in_5), .op_code_0(in_6), .exception(in_7),
    .reg_w_enable(REG_W_ENABLE), .reg_r_enable(REG_R_ENABLE), .data_mem_op(DATA_MEM_OP));
  Alu_Control_Unit alu_control_unit_1 (
    .op_bit_4(in_2), .op_bit_3(in_3), .op_bit_2(in_4), .op_bit_1(in_5), .op_bit_0(in_6), .exception(in_7),
    .alu_enable(ALU_ENABLE), .alu_op_ctrl_bit_2(out_14[2]), .alu_op_ctrl_bit_1(out_14[1]),
    .alu_op_ctrl_bit_0(out_14[0]));
  Pc_Unit_Control pc_unit_control_1 (
    .op_code_4(in_2), .upc_enable(UPC_ENABLE), .op_code_3(in_3), .branch_ctrl(BRANCH_CTRL), .op_code_2(in_4),
    .op_code_1(in_5), .op_code_0(in_6), .zero_flag(d_ff_1_q), .sign_flag(d_ff_2_q), .carry_flag(d_ff_3_q),
    .overflow_flag(d_ff_4_q), .exception(in_7));
  Instr_Mem_Control_Unit instr_mem_control_unit_1 (
    .op_code_4(in_2), .op_code_3(in_3), .op_code_2(in_4), .op_code_1(in_5), .op_code_0(in_6),
    .exception(in_7), .instr_mem_enable(INSTR_MEM_ENABLE));
  Data_Memory_Control_Unit data_memory_control_unit_1 (
    .op_code_4(in_2), .op_code_3(in_3), .op_code_2(in_4), .op_code_1(in_5), .op_code_0(in_6),
    .exception(in_7), .data_l_w(DATA_MEM_L_W), .data_mem_enable(DATA_MEM_ENABLE));
  In_Out_control_unit in_out_control_unit_1 (
    .a(in_2), .I_O_ENABLE(I_O_ENABLE), .b(in_3), .c(in_4), .i_o_op(I_O_OP), .d(in_5),
    .data_in_ctrl(DATA_IN_CTRL), .e(in_6), .exception(in_7));

  // Other names for the same wires on the sheet: CARRY_FLAG = in_9; CLOCK = in_1; EXCEPTION = in_7; OP_BIT_0 = in_6;
  //   OP_BIT_1 = in_5; OP_BIT_2 = in_4; OP_BIT_3 = in_3; OP_BIT_4 = in_2; OVERFLOW_FLAG = in_8; RESET = in_12;
  //   SIGN_FLAG = in_11; ZERO_FLAG = in_10
endmodule

module ALU (
  input  [7:0] ALU_IN1,
  input  ALU_ENABLE,
  input  [2:0] ALU_OPERATION_CTRL,
  input  [7:0] ALU_IN2,
  output [7:0] ALU_RESULT,
  output ZERO_FLAG,
  output SIGN_FLAG,
  output CARRY_FLAG,
  output OVERFLOW_FLAG
);

  wire ADD_CARRY, and_2_out, and_3_out, and_4_out, and_5_out, not_1_out, not_2_out, not_3_out, not_4_out,
       or_2_out, SUB_BORROW;
  wire [2:0] bit_extender_1_out;
  wire [7:0] add_result, and_result, or_result, shl_result, shr_result, sub_result;

  Bit_Extender #(.out_width(3)) bit_extender_1 (.in(ALU_IN2), .out(bit_extender_1_out));
  Adder adder_1 (.a(ALU_IN1), .b(ALU_IN2), .out(add_result), .cout(ADD_CARRY));  // open: cin
  Subtractor subtractor_1 (.a(ALU_IN1), .b(ALU_IN2), .out(sub_result), .bout(SUB_BORROW));  // open: bin
  assign and_result = ALU_IN1 & ALU_IN2;  // AND_Gate and_1, 8 bits wide
  assign or_result = ALU_IN1 | ALU_IN2;  // OR_Gate or_1, 8 bits wide
  Shifter shifter_1 (.in(ALU_IN1), .\dist (bit_extender_1_out), .out(shl_result));
  Shifter #(.shift("lr")) shifter_2 (.in(ALU_IN1), .\dist (bit_extender_1_out), .out(shr_result));
  Multiplexer #(.select(3), .width(8)) multiplexer_1 (
    .in0(add_result), .in1(sub_result), .in2(and_result), .in3(or_result), .in4(shl_result),
    .in5(shr_result), .out(ALU_RESULT), .sel(ALU_OPERATION_CTRL), .en(ALU_ENABLE));  // open: in6, in7
  or or_2 (or_2_out, ALU_RESULT[0], ALU_RESULT[1], ALU_RESULT[2], ALU_RESULT[3], ALU_RESULT[4], ALU_RESULT[5], ALU_RESULT[6], ALU_RESULT[7]);
  not not_1 (not_1_out, ALU_OPERATION_CTRL[0]);
  not not_2 (not_2_out, ALU_IN1[7]);
  not not_3 (not_3_out, ALU_IN2[7]);
  not not_4 (not_4_out, ALU_RESULT[7]);
  not not_5 (ZERO_FLAG, or_2_out);
  and and_2 (and_2_out, SUB_BORROW, ALU_OPERATION_CTRL[0]);
  and and_3 (and_3_out, ADD_CARRY, not_1_out);
  and and_4 (and_4_out, not_2_out, not_3_out, ALU_RESULT[7]);
  or or_3 (OVERFLOW_FLAG, and_4_out, and_5_out);
  and and_5 (and_5_out, ALU_IN1[7], ALU_IN2[7], not_4_out);
  or or_4 (CARRY_FLAG, and_2_out, and_3_out);

  assign SIGN_FLAG = ALU_RESULT[7];

  // Other names for the same wires on the sheet: ALU_IN_1[7:0] = ALU_IN1; ALU_IN_2[7:0] = ALU_IN2
endmodule

module Instruction_management (
  input  [15:0] INSTRUCTION,
  output [4:0] op_code,
  output [2:0] REG_DST,
  output [2:0] REG_SRC1,
  output [2:0] REG_SRC2,
  output [10:0] BRANCH_OFFSET,
  output [7:0] CONST_VALUE
);


  assign BRANCH_OFFSET = INSTRUCTION[10:0];
  assign CONST_VALUE = INSTRUCTION[7:0];
  assign op_code = INSTRUCTION[15:11];
  assign REG_DST = INSTRUCTION[10:8];
  assign REG_SRC1 = INSTRUCTION[7:5];
  assign REG_SRC2 = INSTRUCTION[4:2];

  // Other names for the same wires on the sheet: bit8 = INSTRUCTION[8]; bit9 = INSTRUCTION[9];
  //   bit10 = INSTRUCTION[10]; bit0 = INSTRUCTION[0]; bit1 = INSTRUCTION[1]; bit5 = INSTRUCTION[5];
  //   bit6 = INSTRUCTION[6]; bit7 = INSTRUCTION[7]; bit2 = INSTRUCTION[2]; bit3 = INSTRUCTION[3];
  //   bit4 = INSTRUCTION[4]
endmodule

module Upgrading_pc_unit (
  input  [15:0] PC,
  input  [10:0] BRANCH_OFFSET,
  input  BRANCH_CTRL,
  input  UPC_ENABLE,
  output out_5,
  output [15:0] NEXT_PC
);

  wire [10:0] adder_4_out, controlled_inverter_1_out;
  wire [15:0] adder_1_out, adder_2_out, adder_3_out, adder_5_out, bit_extender_1_out, bit_extender_2_out,
       controlled_inverter_2_out, multiplexer_1_out;

  assign bit_extender_1_out = {{5{1'b0}}, BRANCH_OFFSET};  // Bit_Extender bit_extender_1
  assign controlled_inverter_1_out = BRANCH_OFFSET[10] ? ~BRANCH_OFFSET : 11'bz;  // Controlled_Inverter controlled_inverter_1
  Adder #(.width(16)) adder_1 (.a(PC), .b(16'h1), .out(adder_1_out), .cout(out_5));  // open: cin
  Adder #(.width(16)) adder_2 (.a(PC), .b(bit_extender_1_out), .out(adder_2_out));  // open: cin, cout
  Adder #(.width(16)) adder_3 (.a(PC), .b(adder_5_out), .out(adder_3_out));  // open: cin, cout
  Adder #(.width(11)) adder_4 (.a(controlled_inverter_1_out), .b(11'h1), .out(adder_4_out));  // open: cin, cout
  Multiplexer #(.width(16)) multiplexer_1 (
    .in0(adder_2_out), .in1(adder_3_out), .out(multiplexer_1_out), .sel(BRANCH_OFFSET[10]), .en(1'b1));
  Multiplexer #(.width(16)) multiplexer_2 (
    .in0(adder_1_out), .in1(multiplexer_1_out), .out(NEXT_PC), .sel(BRANCH_CTRL), .en(UPC_ENABLE));
  assign bit_extender_2_out = {{5{1'b0}}, adder_4_out};  // Bit_Extender bit_extender_2
  assign controlled_inverter_2_out = BRANCH_OFFSET[10] ? ~bit_extender_2_out : 16'bz;  // Controlled_Inverter controlled_inverter_2
  Adder #(.width(16)) adder_5 (.a(controlled_inverter_2_out), .b(16'h1), .out(adder_5_out));  // open: cin, cout
endmodule

// REGISTER_FILE
module Register_File (
  input  REG_READ_ENABLE,
  input  CLOCK,
  input  [7:0] DATA_FROM_STACK,
  input  [7:0] DATA_FROM_ALU,
  input  [7:0] CONST_VALUE,
  input  [7:0] DATA_FROM_MEMORY,
  input  [7:0] DATA_FROM_REG,
  input  [2:0] REG_WRITE_CTRL,
  input  [2:0] REG_SRC1,
  input  DATA_MEM_OP,
  input  REG_WRITE_ENABLE,
  input  clock_2,
  input  [2:0] REG_DST,
  input  [2:0] REG_SRC2,
  input  RESET_BUTTON,
  output [7:0] DATA_SRC1,
  output [7:0] DATA_SRC2,
  output [7:0] reg_n_7
);

  wire and_1_out, and_2_out, and_3_out, and_4_out, and_5_out, and_6_out, and_7_out, and_8_out, and_9_out,
       and_10_out, and_11_out, bit_0, bit_1, bit_2, bit_3, bit_4, bit_5, bit_6, bit_7, not_1_out;
  wire [2:0] multiplexer_3_out;
  wire [7:0] DATA_TO_WRITE, reg_0, reg_1, reg_2, reg_3, reg_4, reg_5, reg_6;

  not not_1 (not_1_out, clock_2);
  and and_1 (and_1_out, CLOCK, not_1_out);
  Multiplexer #(.select(3), .width(8)) multiplexer_1 (
    .in0(DATA_FROM_STACK), .in1(DATA_FROM_ALU), .in2(CONST_VALUE), .in3(DATA_FROM_MEMORY),
    .in4(DATA_FROM_REG), .out(DATA_TO_WRITE), .sel(REG_WRITE_CTRL), .en(and_2_out));  // open: in5, in6, in7
  and and_2 (and_2_out, REG_WRITE_ENABLE, and_1_out);
  Demultiplexer #(.select(3)) demultiplexer_1 (
    .out0(bit_0), .out1(bit_1), .out2(bit_2), .out3(bit_3), .out4(bit_4), .out5(bit_5), .out6(bit_6),
    .out7(bit_7), .in(1'b1), .sel(REG_DST), .en(and_2_out));
  and and_3 (and_3_out, clock_2, bit_2);
  and and_4 (and_4_out, clock_2, bit_3);
  and and_5 (and_5_out, clock_2, bit_4);
  and and_6 (and_6_out, clock_2, bit_5);
  and and_7 (and_7_out, clock_2, bit_6);
  and and_8 (and_8_out, clock_2, bit_7);
  Register register_1 (.D(DATA_TO_WRITE), .Q(reg_0), .clk(and_9_out), .clr(RESET_BUTTON));  // open: en
  and and_9 (and_9_out, clock_2, bit_0);
  Register register_2 (.D(DATA_TO_WRITE), .Q(reg_1), .clk(and_10_out), .clr(RESET_BUTTON));  // open: en
  and and_10 (and_10_out, clock_2, bit_1);
  Register register_3 (.D(DATA_TO_WRITE), .Q(reg_2), .clk(and_3_out), .clr(RESET_BUTTON));  // open: en
  Register register_4 (.D(DATA_TO_WRITE), .Q(reg_3), .clk(and_4_out), .clr(RESET_BUTTON));  // open: en
  Register register_5 (.D(DATA_TO_WRITE), .Q(reg_4), .clk(and_5_out), .clr(RESET_BUTTON));  // open: en
  Register register_6 (.D(DATA_TO_WRITE), .Q(reg_5), .clk(and_6_out), .clr(RESET_BUTTON));  // open: en
  Register register_7 (.D(DATA_TO_WRITE), .Q(reg_6), .clk(and_7_out), .clr(RESET_BUTTON));  // open: en
  Register register_8 (.D(DATA_TO_WRITE), .Q(reg_n_7), .clk(and_8_out), .clr(RESET_BUTTON));  // open: en
  and and_11 (and_11_out, CLOCK, clock_2);
  Multiplexer #(.select(3), .width(8)) multiplexer_2 (
    .in0(reg_0), .in1(reg_1), .in2(reg_2), .in3(reg_3), .in4(reg_4), .in5(reg_5), .in6(reg_6), .in7(reg_n_7),
    .out(DATA_SRC1), .sel(multiplexer_3_out), .en(REG_READ_ENABLE));
  Multiplexer #(.width(3)) multiplexer_3 (
    .in0(REG_SRC1), .in1(REG_DST), .out(multiplexer_3_out), .sel(DATA_MEM_OP), .en(1'b1));
  Multiplexer #(.select(3), .width(8)) multiplexer_4 (
    .in0(reg_0), .in1(reg_1), .in2(reg_2), .in3(reg_3), .in4(reg_4), .in5(reg_5), .in6(reg_6), .in7(reg_n_7),
    .out(DATA_SRC2), .sel(REG_SRC2), .en(REG_READ_ENABLE));

  // Other names for the same wires on the sheet: reg_7[7:0] = reg_n_7; RESET = RESET_BUTTON
endmodule

// STACK_FILE
module Stack_File (
  input  [7:0] DATA_FROM_REGISTER_FILE,
  input  CLOCK,
  input  STACK_READ_ENABLE,
  input  STACK_WRITE_ENABLE,
  output [7:0] DATA_FROM_STACK,
  output S_OVERFLOW
);

  wire ADD_OVERFLOW, and_1_out, and_2_out, and_3_out, and_4_out, and_5_out, and_6_out, and_7_out, and_8_out,
       and_9_out, and_10_out, and_11_out, CLOCK_t, not_1_out, s_0, s_1, s_2, s_3, s_4, s_5, s_6, s_7,
       STACK_POINTER_UPDATE_ENABLE, SUB_OVERFLOW;
  wire [2:0] add_stack_1_s0_2, NEW_STACK_POINTER, STACK_POINTER, sub_stack_1_s0_2;
  wire [7:0] DATA_S_0, DATA_S_1, DATA_S_2, DATA_S_3, DATA_S_4, DATA_S_5, DATA_S_6, DATA_S_7;

  Clock clock_1 (.out(CLOCK_t));
  Decoder #(.select(3)) decoder_1 (
    .out0(s_0), .out1(s_1), .out2(s_2), .out3(s_3), .out4(s_4), .out5(s_5), .out6(s_6), .out7(s_7),
    .sel(STACK_POINTER), .en(STACK_WRITE_ENABLE));
  Register register_1 (.D(DATA_FROM_REGISTER_FILE), .Q(DATA_S_0), .clk(and_1_out));  // open: en, clr
  and and_1 (and_1_out, CLOCK_t, s_0);
  Register register_2 (.D(DATA_FROM_REGISTER_FILE), .Q(DATA_S_1), .clk(and_2_out));  // open: en, clr
  and and_2 (and_2_out, CLOCK_t, s_1);
  Register register_3 (.D(DATA_FROM_REGISTER_FILE), .Q(DATA_S_2), .clk(and_3_out));  // open: en, clr
  and and_3 (and_3_out, CLOCK_t, s_2);
  Register register_4 (.D(DATA_FROM_REGISTER_FILE), .Q(DATA_S_3), .clk(and_4_out));  // open: en, clr
  and and_4 (and_4_out, CLOCK_t, s_3);
  Register register_5 (.D(DATA_FROM_REGISTER_FILE), .Q(DATA_S_4), .clk(and_5_out));  // open: en, clr
  and and_5 (and_5_out, CLOCK_t, s_4);
  Register register_6 (.D(DATA_FROM_REGISTER_FILE), .Q(DATA_S_5), .clk(and_6_out));  // open: en, clr
  and and_6 (and_6_out, CLOCK_t, s_5);
  Register register_7 (.D(DATA_FROM_REGISTER_FILE), .Q(DATA_S_6), .clk(and_7_out));  // open: en, clr
  and and_7 (and_7_out, CLOCK_t, s_6);
  Register register_8 (.D(DATA_FROM_REGISTER_FILE), .Q(DATA_S_7), .clk(and_8_out));  // open: en, clr
  and and_8 (and_8_out, CLOCK_t, s_7);
  Multiplexer #(.select(3), .width(8)) multiplexer_1 (
    .in0(DATA_S_0), .in1(DATA_S_1), .in2(DATA_S_2), .in3(DATA_S_3), .in4(DATA_S_4), .in5(DATA_S_5),
    .in6(DATA_S_6), .in7(DATA_S_7), .out(DATA_FROM_STACK), .sel(STACK_POINTER), .en(STACK_READ_ENABLE));
  and and_9 (and_9_out, CLOCK_t, STACK_POINTER_UPDATE_ENABLE);
  Register #(.width(3)) u_STACK_POINTER (.D(NEW_STACK_POINTER), .Q(STACK_POINTER), .clk(and_9_out));  // open: en, clr
  not not_1 (not_1_out, STACK_READ_ENABLE);
  Add_stack add_stack_1 (
    .s2(STACK_POINTER[2]), .s1(STACK_POINTER[1]), .s0(STACK_POINTER[0]), .S2_2(add_stack_1_s0_2[2]),
    .S1_2(add_stack_1_s0_2[1]), .S0_2(add_stack_1_s0_2[0]), .S_OVERFLOW(ADD_OVERFLOW));
  Sub_stack sub_stack_1 (
    .s2(STACK_POINTER[2]), .s1(STACK_POINTER[1]), .s0(STACK_POINTER[0]), .S2_2(sub_stack_1_s0_2[2]),
    .S1_2(sub_stack_1_s0_2[1]), .S0_2(sub_stack_1_s0_2[0]), .SUB_OVERFLOW(SUB_OVERFLOW));
  and and_10 (and_10_out, ADD_OVERFLOW, not_1_out);
  and and_11 (and_11_out, SUB_OVERFLOW, STACK_READ_ENABLE);
  or or_1 (STACK_POINTER_UPDATE_ENABLE, STACK_READ_ENABLE, STACK_WRITE_ENABLE);
  Multiplexer #(.width(3)) multiplexer_2 (
    .in0(add_stack_1_s0_2), .in1(sub_stack_1_s0_2), .out(NEW_STACK_POINTER), .sel(STACK_READ_ENABLE),
    .en(STACK_POINTER_UPDATE_ENABLE));
  or or_2 (S_OVERFLOW, and_10_out, and_11_out);

  // Other names for the same wires on the sheet: S_TO_WRITE[7:0] = DATA_FROM_REGISTER_FILE
endmodule

module Add_stack (
  input  s2,
  input  s1,
  input  s0,
  output S2_2,
  output S1_2,
  output S0_2,
  output S_OVERFLOW
);

  wire and_1_out, and_3_out, and_4_out, not_1_out, not_2_out;

  and and_1 (and_1_out, s1, s0);
  not not_1 (not_1_out, s1);
  not not_2 (not_2_out, s0);
  not not_3 (S0_2, s0);
  and and_2 (S_OVERFLOW, s2, s1, s0);
  or or_1 (S2_2, and_1_out, s2);
  and and_3 (and_3_out, not_1_out, s0);
  and and_4 (and_4_out, s1, not_2_out);
  or or_2 (S1_2, and_3_out, and_4_out);
endmodule

module Sub_stack (
  input  s2,
  input  s1,
  input  s0,
  output S2_2,
  output S1_2,
  output S0_2,
  output SUB_OVERFLOW
);

  wire and_1_out, and_2_out, and_3_out, and_4_out, not_1_out, not_2_out, not_4_out, not_5_out, not_6_out;

  and and_1 (and_1_out, s2, s0);
  and and_2 (and_2_out, s2, s1);
  not not_1 (not_1_out, s1);
  not not_2 (not_2_out, s0);
  not not_3 (S0_2, s0);
  not not_4 (not_4_out, s2);
  not not_5 (not_5_out, s1);
  not not_6 (not_6_out, s0);
  or or_1 (S2_2, and_1_out, and_2_out);
  and and_3 (and_3_out, not_1_out, not_2_out);
  and and_4 (and_4_out, s1, s0);
  and and_5 (SUB_OVERFLOW, not_4_out, not_5_out, not_6_out);
  or or_2 (S1_2, and_3_out, and_4_out);
endmodule

module Data_memory_management (
  input  [7:0] DATA_TO_MEMORY,
  input  [7:0] const_value,
  input  [7:0] reg_n_7,
  output [7:0] DATA_TO_MEMORY_2,
  output [15:0] addr
);


  assign addr = {reg_n_7, const_value};
  assign DATA_TO_MEMORY_2 = DATA_TO_MEMORY;

  // Notes on the sheet:
  //   from REG_SRC1
endmodule

module tmp (
  input  main_clock,
  input  clock_2,
  output x
);

  and and_1 (x, main_clock, clock_2);
endmodule

// CLOCK_UNIT
module Clock_unit (
  output MAIN_CLOCK,
  output CLOCK_2
);

  Clock clock_1 (.out(CLOCK_2));
  Counter #(.width(1), .max('h1)) counter_1 (
    .D(CLOCK_2), .Q(MAIN_CLOCK), .clk(CLOCK_2));  // open: load, count, carry, clr
endmodule

module Alu_Control_Unit (
  input  op_bit_4,
  input  op_bit_3,
  input  op_bit_2,
  input  op_bit_1,
  input  op_bit_0,
  input  exception,
  output alu_enable,
  output alu_op_ctrl_bit_2,
  output alu_op_ctrl_bit_1,
  output alu_op_ctrl_bit_0
);

  wire and_1_out, and_2_out, and_3_out, and_4_out, and_5_out, and_6_out, and_7_out, and_8_out, not_1_out,
       not_2_out, not_3_out, not_4_out, not_5_out, not_6_out, not_7_out, not_8_out, not_9_out, not_10_out,
       not_11_out, not_12_out, not_13_out, not_14_out, not_15_out;

  not not_1 (not_1_out, op_bit_4);
  not not_2 (not_2_out, op_bit_3);
  not not_3 (not_3_out, exception);
  not not_4 (not_4_out, op_bit_4);
  not not_5 (not_5_out, op_bit_3);
  not not_6 (not_6_out, exception);
  not not_7 (not_7_out, op_bit_4);
  not not_8 (not_8_out, op_bit_3);
  not not_9 (not_9_out, exception);
  not not_10 (not_10_out, op_bit_1);
  not not_11 (not_11_out, op_bit_0);
  not not_12 (not_12_out, op_bit_1);
  not not_13 (not_13_out, op_bit_0);
  not not_14 (not_14_out, op_bit_2);
  not not_15 (not_15_out, op_bit_0);
  and and_1 (and_1_out, op_bit_2, op_bit_1);
  and and_2 (and_2_out, not_1_out, not_2_out, op_bit_0, not_3_out);
  and and_3 (and_3_out, not_4_out, not_5_out, op_bit_1, not_6_out);
  and and_4 (and_4_out, not_7_out, not_8_out, op_bit_2, not_9_out);
  and and_5 (and_5_out, op_bit_2, not_10_out, op_bit_0);
  and and_6 (and_6_out, op_bit_2, op_bit_1, not_11_out);
  and and_7 (and_7_out, not_12_out, not_13_out);
  and and_8 (and_8_out, not_14_out, op_bit_1, op_bit_0);
  or or_1 (alu_op_ctrl_bit_0, not_15_out, and_1_out);
  or or_2 (alu_enable, and_2_out, and_3_out, and_4_out);
  or or_3 (alu_op_ctrl_bit_2, and_5_out, and_6_out);
  or or_4 (alu_op_ctrl_bit_1, and_7_out, and_8_out);
endmodule

module Stack_Control_Unit (
  input  op_bit_4,
  input  op_bit_3,
  input  op_bit_2,
  input  op_bit_1,
  input  op_bit_0,
  input  exception,
  output stack_write_enable,
  output stack_read_enable
);

  wire not_1_out, not_2_out, not_3_out, not_4_out, not_5_out, not_6_out, not_7_out;

  not not_1 (not_1_out, op_bit_4);
  not not_2 (not_2_out, op_bit_1);
  not not_3 (not_3_out, exception);
  not not_4 (not_4_out, op_bit_4);
  not not_5 (not_5_out, op_bit_1);
  not not_6 (not_6_out, op_bit_0);
  not not_7 (not_7_out, exception);
  and and_1 (stack_write_enable, not_1_out, op_bit_3, op_bit_2, not_2_out, op_bit_0, not_3_out);
  and and_2 (stack_read_enable, not_4_out, op_bit_3, op_bit_2, not_5_out, not_6_out, not_7_out);
endmodule

module Pc_Unit_Control (
  input  op_code_4,
  input  op_code_3,
  input  op_code_2,
  input  op_code_1,
  input  op_code_0,
  input  zero_flag,
  input  sign_flag,
  input  carry_flag,
  input  overflow_flag,
  input  exception,
  output upc_enable,
  output branch_ctrl
);

  wire and_1_out, and_2_out, and_3_out, and_4_out, and_5_out, not_2_out, not_3_out, not_4_out, not_5_out,
       not_6_out, not_7_out, not_8_out, not_9_out, not_10_out, not_11_out, or_1_out;

  not not_1 (upc_enable, exception);
  not not_2 (not_2_out, op_code_1);
  not not_3 (not_3_out, op_code_0);
  not not_4 (not_4_out, op_code_1);
  not not_5 (not_5_out, op_code_0);
  not not_6 (not_6_out, overflow_flag);
  not not_7 (not_7_out, op_code_0);
  not not_8 (not_8_out, sign_flag);
  and and_1 (and_1_out, not_2_out, not_3_out, zero_flag);
  and and_2 (and_2_out, not_4_out, op_code_0, carry_flag);
  and and_3 (and_3_out, op_code_1, not_5_out, sign_flag, not_6_out);
  and and_4 (and_4_out, op_code_1, not_7_out, not_8_out, overflow_flag);
  and and_5 (and_5_out, op_code_1, op_code_0);
  not not_9 (not_9_out, exception);
  not not_10 (not_10_out, op_code_4);
  not not_11 (not_11_out, op_code_2);
  or or_1 (or_1_out, and_1_out, and_2_out, and_3_out, and_4_out, and_5_out);
  and and_6 (branch_ctrl, not_9_out, not_10_out, op_code_3, not_11_out, or_1_out);
endmodule

module Instr_Mem_Control_Unit (
  input  op_code_4,
  input  op_code_3,
  input  op_code_2,
  input  op_code_1,
  input  op_code_0,
  input  exception,
  output instr_mem_enable
);

  wire and_1_out, and_2_out, and_3_out, and_4_out, and_5_out, not_1_out, not_2_out, not_3_out, not_4_out,
       not_5_out;

  not not_1 (not_1_out, exception);
  not not_2 (not_2_out, exception);
  not not_3 (not_3_out, exception);
  not not_4 (not_4_out, exception);
  not not_5 (not_5_out, exception);
  and and_1 (and_1_out, op_code_0, not_1_out);
  and and_2 (and_2_out, op_code_1, not_2_out);
  and and_3 (and_3_out, op_code_2, not_3_out);
  and and_4 (and_4_out, op_code_3, not_4_out);
  and and_5 (and_5_out, op_code_4, not_5_out);
  or or_1 (instr_mem_enable, and_1_out, and_2_out, and_3_out, and_4_out, and_5_out);
endmodule

module Exception_Control_Unit (
  input  op_code_4,
  input  op_code_3,
  input  op_code_2,
  input  op_code_1,
  input  op_code_0,
  input  main_clock,
  input  clock_2,
  input  overflow_flag,
  input  pc_overflow,
  input  stack_overflow,
  output exception
);

  wire and_1_out, and_2_out, and_3_out, and_4_out, and_5_out, and_6_out, not_1_out, not_2_out, not_3_out,
       not_4_out, not_5_out, not_6_out, not_7_out, not_8_out, not_9_out, not_10_out;

  not not_1 (not_1_out, clock_2);
  not not_2 (not_2_out, clock_2);
  not not_3 (not_3_out, op_code_3);
  not not_4 (not_4_out, op_code_2);
  not not_5 (not_5_out, clock_2);
  not not_6 (not_6_out, op_code_1);
  not not_7 (not_7_out, op_code_3);
  not not_8 (not_8_out, op_code_2);
  not not_9 (not_9_out, clock_2);
  not not_10 (not_10_out, op_code_0);
  and and_1 (and_1_out, main_clock, not_1_out, stack_overflow);
  and and_2 (and_2_out, main_clock, not_2_out, pc_overflow);
  and and_3 (and_3_out, not_3_out, main_clock, not_4_out, not_5_out, not_6_out, op_code_0, overflow_flag);
  and and_4 (and_4_out, not_7_out, main_clock, not_8_out, not_9_out, op_code_1, not_10_out, overflow_flag);
  and and_5 (and_5_out, op_code_4, main_clock);
  and and_6 (and_6_out, op_code_4, op_code_3);
  or or_1 (exception, and_1_out, and_2_out, and_3_out, and_4_out, and_5_out, and_6_out);
endmodule

module Reg_File_Control_Unit (
  input  op_code_4,
  input  op_code_3,
  input  op_code_2,
  input  op_code_1,
  input  op_code_0,
  input  exception,
  output reg_w_ctrl_2,
  output reg_w_ctrl_1,
  output reg_w_ctrl_0,
  output reg_w_enable,
  output reg_r_enable,
  output data_mem_op
);

  wire and_1_out, and_3_out, and_4_out, and_5_out, and_6_out, and_7_out, and_8_out, and_9_out, and_10_out,
       and_11_out, and_12_out, and_13_out, and_14_out, and_15_out, not_1_out, not_3_out, not_4_out,
       not_5_out, not_6_out, not_7_out, not_8_out, not_9_out, not_10_out, not_11_out, not_12_out, not_13_out,
       not_14_out, not_15_out, not_16_out, not_17_out, not_18_out, not_19_out, not_20_out, not_21_out,
       not_22_out, not_23_out, not_24_out, not_25_out, not_26_out, not_27_out, not_28_out, not_29_out,
       not_30_out, not_31_out, not_32_out, not_33_out, not_34_out, not_35_out, not_36_out, not_37_out,
       not_38_out, not_39_out, not_40_out, not_41_out, not_42_out, not_43_out, not_44_out;

  not not_1 (not_1_out, op_code_0);
  and and_1 (and_1_out, op_code_3, op_code_0);
  not not_2 (reg_w_ctrl_0, op_code_3);
  not not_3 (not_3_out, op_code_4);
  not not_4 (not_4_out, op_code_3);
  not not_5 (not_5_out, op_code_1);
  not not_6 (not_6_out, exception);
  not not_7 (not_7_out, op_code_4);
  not not_8 (not_8_out, op_code_3);
  not not_9 (not_9_out, op_code_2);
  not not_10 (not_10_out, exception);
  not not_11 (not_11_out, op_code_3);
  not not_12 (not_12_out, op_code_2);
  not not_13 (not_13_out, exception);
  not not_14 (not_14_out, op_code_4);
  not not_15 (not_15_out, op_code_0);
  not not_16 (not_16_out, exception);
  not not_17 (not_17_out, op_code_4);
  not not_18 (not_18_out, exception);
  not not_19 (not_19_out, op_code_3);
  not not_20 (not_20_out, op_code_2);
  not not_21 (not_21_out, op_code_1);
  not not_22 (not_22_out, op_code_0);
  not not_23 (not_23_out, exception);
  not not_24 (not_24_out, op_code_3);
  not not_25 (not_25_out, op_code_2);
  not not_26 (not_26_out, op_code_1);
  not not_27 (not_27_out, exception);
  not not_28 (not_28_out, op_code_4);
  not not_29 (not_29_out, op_code_3);
  not not_30 (not_30_out, exception);
  not not_31 (not_31_out, op_code_3);
  not not_32 (not_32_out, op_code_2);
  not not_33 (not_33_out, op_code_0);
  not not_34 (not_34_out, exception);
  not not_35 (not_35_out, op_code_4);
  not not_36 (not_36_out, op_code_3);
  not not_37 (not_37_out, exception);
  not not_38 (not_38_out, op_code_4);
  not not_39 (not_39_out, op_code_1);
  not not_40 (not_40_out, exception);
  not not_41 (not_41_out, op_code_4);
  not not_42 (not_42_out, op_code_0);
  not not_43 (not_43_out, exception);
  not not_44 (not_44_out, op_code_1);
  and and_2 (reg_w_ctrl_2, op_code_3, op_code_1, not_1_out);
  or or_1 (reg_w_ctrl_1, and_1_out, op_code_4);
  and and_3 (and_3_out, not_3_out, not_4_out, not_5_out, op_code_0, not_6_out);
  and and_4 (and_4_out, not_7_out, not_8_out, not_9_out, op_code_1, not_10_out);
  and and_5 (and_5_out, not_11_out, not_12_out, op_code_1, op_code_0, not_13_out);
  and and_6 (and_6_out, not_14_out, op_code_2, not_15_out, not_16_out);
  and and_7 (and_7_out, not_17_out, op_code_3, op_code_2, op_code_1, not_18_out);
  and and_8 (and_8_out, op_code_4, not_19_out, not_20_out, not_21_out, not_22_out, not_23_out);
  and and_9 (and_9_out, not_24_out, not_25_out, not_26_out, op_code_0, not_27_out);
  and and_10 (and_10_out, not_28_out, not_29_out, op_code_1, not_30_out);
  and and_11 (and_11_out, not_31_out, not_32_out, op_code_1, not_33_out, not_34_out);
  and and_12 (and_12_out, not_35_out, not_36_out, op_code_2, not_37_out);
  and and_13 (and_13_out, not_38_out, op_code_2, not_39_out, op_code_0, not_40_out);
  and and_14 (and_14_out, not_41_out, op_code_2, op_code_1, not_42_out, not_43_out);
  and and_15 (and_15_out, op_code_3, not_44_out);
  or or_2 (reg_w_enable, and_3_out, and_4_out, and_5_out, and_6_out, and_7_out, and_8_out);
  or or_3 (reg_r_enable, and_9_out, and_10_out, and_11_out, and_12_out, and_13_out, and_14_out);
  or or_4 (data_mem_op, and_15_out, op_code_4);
endmodule

module Data_Memory_Control_Unit (
  input  op_code_4,
  input  op_code_3,
  input  op_code_2,
  input  op_code_1,
  input  op_code_0,
  input  exception,
  output data_l_w,
  output data_mem_enable
);

  wire not_1_out, not_2_out, not_3_out, not_4_out;

  not not_1 (not_1_out, op_code_3);
  not not_2 (not_2_out, op_code_2);
  not not_3 (not_3_out, op_code_1);
  not not_4 (not_4_out, exception);
  and and_1 (data_mem_enable, op_code_4, not_1_out, not_2_out, not_3_out, not_4_out);

  assign data_l_w = op_code_0;
endmodule

module In_Out_control_unit (
  input  a,
  input  b,
  input  c,
  input  d,
  input  e,
  input  exception,
  output I_O_ENABLE,
  output i_o_op,
  output data_in_ctrl
);

  wire not_1_out, not_2_out, not_3_out;

  not not_1 (not_1_out, b);
  not not_2 (not_2_out, c);
  not not_3 (not_3_out, exception);
  not not_4 (i_o_op, e);
  and and_1 (I_O_ENABLE, a, not_1_out, not_2_out, not_3_out);

  assign data_in_ctrl = 1'b1;
endmodule

module CPU_8_BIT (
  input  ON_BUTTON
);

  wire and_1_out, CLOCK_2, main_1_i_o_enable, main_1_i_o_op, main_1_out_7, main_1_out_8, MAIN_CLOCK,
       MEMORY_RESET_out, not_1_out, not_2_out, RESET_BUTTON_out;
  wire [7:0] controlled_buffer_1_out, eventuale_periferica, main_1_data_mem_data, main_1_data_to_out,
       multiplexer_1_out, ram_2_data;
  wire [15:0] main_1_data_mem_addr, main_1_instr_mem_addr, ram_1_data;

  Clock_unit clock_unit_1 (.MAIN_CLOCK(MAIN_CLOCK), .CLOCK_2(CLOCK_2));
  Button RESET_BUTTON (.out(RESET_BUTTON_out));
  RAM #(.addrWidth(16), .dataWidth(16), .bus("separate")) ram_1 (
    .addr(main_1_instr_mem_addr), .data(ram_1_data), .str(1'b0), .sel(ON_BUTTON), .clk(MAIN_CLOCK),
    .ld(ON_BUTTON), .clr(MEMORY_RESET_out));  // open: din
  Button MEMORY_RESET (.out(MEMORY_RESET_out));
  main main_1 (
    .RESET_BUTTON(RESET_BUTTON_out), .CLOCK_2(CLOCK_2), .MAIN_CLOCK(MAIN_CLOCK),
    .INSTR_MEM_ADDR(main_1_instr_mem_addr), .INSTRUCTION(ram_1_data), .DATA_MEM_ADDR(main_1_data_mem_addr),
    .DATA_MEM_DATA(main_1_data_mem_data), .out_8(main_1_out_8), .out_7(main_1_out_7),
    .in_3(multiplexer_1_out), .I_O_ENABLE(main_1_i_o_enable), .I_O_OP(main_1_i_o_op),
    .DATA_TO_OUT(main_1_data_to_out), .ON_BUTTON(ON_BUTTON));  // open: out_10, DATA_IN_OUT_CTRL
  and and_1 (and_1_out, main_1_i_o_enable, main_1_i_o_op);
  assign controlled_buffer_1_out = and_1_out ? main_1_data_to_out : 8'bz;  // Controlled_Buffer controlled_buffer_1
  not not_1 (not_1_out, main_1_i_o_op);
  Multiplexer #(.width(8)) multiplexer_1 (
    .in0(ram_2_data), .in1(eventuale_periferica), .out(multiplexer_1_out), .sel(not_1_out), .en(1'b1));
  RAM #(.addrWidth(16), .bus("separate")) ram_2 (
    .addr(main_1_data_mem_addr), .din(main_1_data_mem_data), .data(ram_2_data), .str(main_1_out_7),
    .sel(main_1_out_8), .clk(MAIN_CLOCK), .ld(not_2_out), .clr(MEMORY_RESET_out));
  not not_2 (not_2_out, main_1_out_7);
  Hex_Digit_Display hex_digit_display_1 (.value(controlled_buffer_1_out[7:4]));  // open: dp
  Hex_Digit_Display hex_digit_display_2 (.value(controlled_buffer_1_out[3:0]));  // open: dp
  Register register_1 (.D(controlled_buffer_1_out), .clk(MAIN_CLOCK));  // open: en, Q, clr

  // Other names for the same wires on the sheet: ON = ON_BUTTON
endmodule
